# Fritzing sketch circuit (saved by Fritzing 0.9.3b)
breadboards: 2

parts:
  Part1 = Arduino Uno (Rev3)
  Part2 = Arduino Due (Rev2b)
  U1 = MLX90614 [package=to-39]
  R1 = Resistor [tolerance=±5% resistance=220 package=THT]
  R2 = Resistor [tolerance=±5% resistance=220 package=THT]
  S1 = Pushbutton [package="[SMD]"]
  Generic_4x4_button_keypad1 = Generic 4x4 Keypad  # not connected
  R3 = TRIMPOT [package=trimpot_pth_s3_lock]  # not connected
  LCD1 = LCD screen

nets:
  N1: Part1.A4/SDA, U1.VSS, R1.Pin_0
  N2: Part1.A5/SCL, U1.VDD, R2.Pin_0
  N3: Part1.D2, S1.Pin_1, S1.Pin_2
  N4: Part1.3V3, U1.SCL_VZ, R1.Pin_1, R2.Pin_1
  N5: Part1.GND, U1.PWM_SDA, S1.Pin_3, S1.Pin_4
  5V: Part2.5V, LCD1.VDD, LCD1.LED+
  GND: Part2.GND, LCD1.VSS, LCD1.R/W, LCD1.LED-
  N6: Part2.D8_PWM, LCD1.DB7
  N7: Part2.D9_PWM, LCD1.DB6
  N8: Part2.D10_PWM/SS0, LCD1.DB5
  N9: Part2.D11_PWM, LCD1.DB4
  N10: Part2.D12_PWM, LCD1.E
  N11: Part2.D13_PWM, LCD1.RS

custom parts:
  Generic 4x4 Keypad: generic 4x4 keypad 4 rows of four 6 mm tact switches cheap and nasty but works
